# Fritzing sketch Suntracker_Sensor (saved by Fritzing 0.9.3b)
circuit board: 4.11cm x 2.54cm
perfboards: 1

parts:
  R7 = Resistor [tolerance=±5% resistance=22k package=THT]
  R8 = Resistor [tolerance=±5% resistance=22k package=THT]
  R9 = Resistor [tolerance=±5% resistance=22k package=THT]
  LDRRight = Photocell (LDR) [package=THT]
  LDRTop = Photocell (LDR) [package=THT]
  LDRLeft = Photocell (LDR) [package=THT]

nets:
  N1: R7.Pin_0, R8.Pin_0, R9.Pin_0
  N2: R7.Pin_1, LDRRight.pin_0
  N3: R8.Pin_1, LDRTop.pin_0
  N4: R9.Pin_1, LDRLeft.pin_0
  N5: LDRRight.pin_1, LDRTop.pin_1, LDRLeft.pin_1
